// Logisim project 382Project2.circ as structural Verilog: 1 circuit, main circuit main
module main (
);

  wire and_1_out, and_2_out, and_3_out, and_4_out, clock_1_out, clock_2_out, decoder_1_out0, decoder_1_out1,
       decoder_1_out2, decoder_1_out3, not_1_out;
  wire [1:0] multiplexer_1_out, rom_1_data_3, rom_1_data_4;
  wire [4:0] rom_1_data_2;
  wire [7:0] adder_2_out, bit_extender_1_out, multiplexer_2_out, multiplexer_3_out, multiplexer_4_out,
       multiplexer_5_out, ram_1_dout, register_2_q, register_3_q, register_4_q, register_5_q,
       subtractor_1_out;
  wire [10:0] rom_1_data;
  wire [15:0] adder_1_out, register_1_q;

  Clock clock_1 (.out(clock_1_out));
  Register #(.width(16)) register_1 (.D(adder_1_out), .en(1'b1), .clk(clock_1_out), .Q(register_1_q));  // open: clr
  ROM #(.addrWidth(16), .dataWidth(16)) rom_1 (
    .addr(register_1_q),
    .data({rom_1_data_2, rom_1_data[10], rom_1_data_4[0], rom_1_data[8:7], rom_1_data_3, rom_1_data[4:3], rom_1_data_4[1], rom_1_data[1:0]}));
  Adder #(.width(16)) adder_1 (.a(register_1_q), .b(16'h1), .out(adder_1_out));  // open: cin, cout
  assign bit_extender_1_out = {{3{1'b0}}, rom_1_data_2};  // Bit_Extender bit_extender_1
  Multiplexer #(.width(2)) multiplexer_1 (
    .in0({rom_1_data[3], rom_1_data[4]}), .in1({rom_1_data[7], rom_1_data[8]}), .out(multiplexer_1_out),
    .sel(rom_1_data[1]));
  Decoder #(.select(2)) decoder_1 (
    .out0(decoder_1_out0), .out1(decoder_1_out1), .out2(decoder_1_out2), .out3(decoder_1_out3),
    .sel({rom_1_data[3], rom_1_data[4]}));  // open: en
  and and_1 (and_1_out, rom_1_data[0], decoder_1_out3);
  and and_2 (and_2_out, rom_1_data[0], decoder_1_out0);
  and and_3 (and_3_out, rom_1_data[0], decoder_1_out1);
  and and_4 (and_4_out, rom_1_data[0], decoder_1_out2);
  Clock clock_2 (.out(clock_2_out));
  Register register_2 (.D(multiplexer_5_out), .en(and_2_out), .clk(clock_2_out), .Q(register_2_q));  // open: clr
  Register register_3 (.D(multiplexer_5_out), .en(and_3_out), .clk(clock_2_out), .Q(register_3_q));  // open: clr
  Register register_4 (.D(multiplexer_5_out), .en(and_4_out), .clk(clock_2_out), .Q(register_4_q));  // open: clr
  Register register_5 (.D(multiplexer_5_out), .en(and_1_out), .clk(clock_2_out), .Q(register_5_q));  // open: clr
  Hex_Digit_Display hex_digit_display_1 (.value(register_2_q[7:4]));  // open: dp
  Hex_Digit_Display hex_digit_display_2 (.value(register_2_q[3:0]));  // open: dp
  Hex_Digit_Display hex_digit_display_3 (.value(register_3_q[7:4]));  // open: dp
  Multiplexer #(.select(2), .width(8)) multiplexer_2 (
    .in0(register_2_q), .in1(register_3_q), .in2(register_4_q), .in3(register_5_q), .out(multiplexer_2_out),
    .sel(rom_1_data_3));
  Multiplexer #(.select(2), .width(8)) multiplexer_3 (
    .in0(register_2_q), .in1(register_3_q), .in2(register_4_q), .in3(register_5_q), .out(multiplexer_3_out),
    .sel(multiplexer_1_out));
  Hex_Digit_Display hex_digit_display_4 (.value(register_3_q[3:0]));  // open: dp
  Hex_Digit_Display hex_digit_display_5 (.value(register_4_q[7:4]));  // open: dp
  Hex_Digit_Display hex_digit_display_6 (.value(register_4_q[3:0]));  // open: dp
  Adder adder_2 (.a(multiplexer_2_out), .b(multiplexer_3_out), .out(adder_2_out));  // open: cin, cout
  Hex_Digit_Display hex_digit_display_7 (.value(register_5_q[7:4]));  // open: dp
  Subtractor subtractor_1 (.a(multiplexer_2_out), .b(multiplexer_3_out), .out(subtractor_1_out));  // open: bin, bout
  Hex_Digit_Display hex_digit_display_8 (.value(register_5_q[3:0]));  // open: dp
  Multiplexer #(.select(2), .width(8)) multiplexer_4 (
    .in0(adder_2_out), .in1(bit_extender_1_out), .in2(subtractor_1_out), .in3(multiplexer_2_out),
    .out(multiplexer_4_out), .sel(rom_1_data_4));
  RAM ram_1 (
    .addr(multiplexer_4_out), .we(not_1_out), .oe(1'b1), .clk(clock_1_out), .din(multiplexer_3_out),
    .dout(ram_1_dout));
  not not_1 (not_1_out, rom_1_data[0]);
  Multiplexer #(.width(8)) multiplexer_5 (
    .in0(multiplexer_4_out), .in1(ram_1_dout), .out(multiplexer_5_out), .sel(rom_1_data[10]));

  // Notes on the sheet:
  //   Tyler Hackett
  //   Partner: Justin Gajewski
  //   CPU: Please Give Us 110+
  //   I pledge my honor that I have abided by the Stevens Honor Sytsem
  //   Instr Mem
  //   contents of rom_1 (hex, n*v repeats v):
  //   f201 a211 4209 107 103 244 66d 645 17b
  //   Write Reg
  //   RegWrite
  //   Register File
  //   RegReg2
  //   RegData1
  //   ReadReg1
  //   RegDataW
  //   ALU
  //   Mem W/R
  //   Reg2
  //   Data Mem
endmodule
